// Logisim project 2BCD.circ as structural Verilog: 4 circuits, main circuit main
module main (
  input  [6:0] Binary_in,
  output Sign,
  output [3:0] Units,
  output [3:0] Tenth
);

  _2_BCD u_2_bcd_1 (.out_2(Sign), .Binary_in(Binary_in), .Units(Tenth), .Tenth(Units));
endmodule

module _2_BCD (
  input  [6:0] Binary_in,
  output out_2,
  output [3:0] Units,
  output [3:0] Tenth
);

  wire add_bcd_2_out_5, add_bcd_3_out_5, and_1_out, and_2_out, check_bcd_1_out_2, check_bcd_2_out_2,
       or_1_out, or_2_out, sub_1_ind, sub_2_ind, sub_3_ind;
  wire [2:0] add_bcd_1_out_4, add_bcd_2_out_4, add_bcd_3_out_4, multiplexer_2_out;
  wire [2:1] multiplexer_1_out;
  wire [2:2] multiplexer_1_out_2;

  Add_BCD add_bcd_1 (.out_4(add_bcd_1_out_4), .B(3'b011), .A(Binary_in[5:3]), .out_5(Tenth[2]));  // open: in_3
  Sub sub_1 (.A(Binary_in[5:3]), .B(3'b100), .Ind(sub_1_ind));  // open: out_4, Flag
  Multiplexer #(.width(3), .enable("false")) multiplexer_1 (
    .in0(Binary_in[4:2]), .in1({add_bcd_1_out_4[1:0], Binary_in[2]}),
    .out({multiplexer_1_out_2[2], multiplexer_1_out}), .sel(sub_1_ind));
  Check_BCD check_bcd_1 (.out_2(check_bcd_1_out_2), .in_1({multiplexer_1_out_2[2], multiplexer_1_out}));
  and and_1 (and_1_out, check_bcd_1_out_2, add_bcd_1_out_4[2]);
  Add_BCD add_bcd_2 (
    .out_4(add_bcd_2_out_4), .B(3'b011), .A({multiplexer_1_out_2[2], multiplexer_1_out}),
    .out_5(add_bcd_2_out_5));  // open: in_3
  Sub sub_2 (.A({multiplexer_1_out_2[2], multiplexer_1_out}), .B(3'b100), .Ind(sub_2_ind));  // open: out_4, Flag
  Multiplexer #(.width(3), .enable("false")) multiplexer_2 (
    .in0({multiplexer_1_out, Binary_in[1]}), .in1({add_bcd_2_out_4[1:0], Binary_in[1]}),
    .out(multiplexer_2_out), .sel(or_1_out));
  or or_1 (or_1_out, sub_2_ind, and_1_out);
  Check_BCD check_bcd_2 (.out_2(check_bcd_2_out_2), .in_1(multiplexer_2_out));
  Add_BCD add_bcd_3 (
    .out_4(add_bcd_3_out_4), .B(3'b011), .A(multiplexer_2_out), .out_5(add_bcd_3_out_5));  // open: in_3
  and and_2 (and_2_out, check_bcd_2_out_2, add_bcd_2_out_4[2]);
  or or_2 (or_2_out, sub_3_ind, and_2_out);
  Sub sub_3 (.A(multiplexer_2_out), .B(3'b100), .Ind(sub_3_ind));  // open: out_4, Flag
  Multiplexer #(.width(3), .enable("false")) multiplexer_3 (
    .in0(multiplexer_2_out), .in1(add_bcd_3_out_4), .out(Units[3:1]), .sel(or_2_out));
  or or_3 (Tenth[0], add_bcd_3_out_5, and_2_out);
  or or_4 (Tenth[1], add_bcd_2_out_5, and_1_out);

  assign out_2 = Binary_in[6];
  assign Tenth[3] = 1'b0;
  assign Units[0] = Binary_in[0];
endmodule

module Add_BCD (
  input  [2:0] A,
  input  [2:0] B,
  input  in_3,
  output [2:0] out_4,
  output out_5
);

  wire adder_1_cout, adder_2_cout;

  Adder #(.width(1)) adder_1 (.a(A[0]), .b(B[0]), .out(out_4[0]), .cin(in_3), .cout(adder_1_cout));
  Adder #(.width(1)) adder_2 (.a(A[1]), .b(B[1]), .out(out_4[1]), .cin(adder_1_cout), .cout(adder_2_cout));
  Adder #(.width(1)) adder_3 (.a(A[2]), .b(B[2]), .out(out_4[2]), .cin(adder_2_cout), .cout(out_5));
endmodule

module Check_BCD (
  input  [2:0] in_1,
  output out_2
);

  nor nor_1 (out_2, in_1[1], in_1[2]);
endmodule
