// Logisim project Division.circ as structural Verilog
module main (
  input  [3:0] A,
  input  [3:0] B,
  output Zero,
  output Div_by_zero
);

  wire n7404_1_p2, n7404_1_p4, n7404_1_p5, n7432_1_p3, n7432_1_p4, n7432_1_p5, n7432_1_p7, n7432_1_p8,
       n7432_2_p3, one_check_out_2;

  // _7432 7432_1: pin names not known; wires that end beside it: 1'b0, 1'b1, n7432_1_p3, n7432_1_p4, n7432_1_p5, n7432_1_p5, n7432_1_p7, n7432_1_p8, B[2:0], A[2:0], n7432_1_p3, n7432_1_p4, n7432_1_p7
  Zero_Flag Zero_Flag (.out_2(Div_by_zero), .in_1(B));
  one_check one_check (.in_1(B), .out_2(one_check_out_2));
  // _7432 7432_2: pin names not known; wires that end beside it: Div_by_zero, n7432_1_p8, n7432_2_p3, 1'b0, 1'b1
  // _7404 7404_1: pin names not known; wires that end beside it: n7432_2_p3, n7404_1_p2, one_check_out_2, n7404_1_p4, n7404_1_p5, Zero, 1'b0, 1'b1
  // _7408 7408_1: pin names not known; wires that end beside it: n7404_1_p2, n7404_1_p4, n7404_1_p5, 1'b1

  // Notes on the sheet:
  //   Subs
endmodule

module Zero_Flag (
  input  [3:0] in_1,
  output out_2
);

  wire n7432_1_p3, n7432_1_p6, n7432_1_p11;

  // _7432 7432_1: pin names not known; wires that end beside it: in_1[0], in_1[1], n7432_1_p3, n7432_1_p3, in_1[2], n7432_1_p6, 1'b0, 1'b1, n7432_1_p6, in_1[3], n7432_1_p11
  // _7404 7404_1: pin names not known; wires that end beside it: n7432_1_p11, out_2, 1'b0, 1'b1
endmodule

module one_check (
  input  [3:0] in_1,
  output out_2
);

  wire n7404_1_p2, n7404_1_p4, n7408_1_p3, n7408_1_p6;

  // _7404 7404_1: pin names not known; wires that end beside it: in_1[1], n7404_1_p2, in_1[2], n7404_1_p4, 1'b0, 1'b1
  // _7408 7408_1: pin names not known; wires that end beside it: 1'b1, in_1[0], n7408_1_p3, n7408_1_p3, n7404_1_p2, n7408_1_p6, 1'b0, 1'b1, n7408_1_p6, n7404_1_p4, out_2
endmodule
