// Logisim project Multiplication.circ as structural Verilog: 1 circuit, main circuit main
module main (
  input  [3:0] in_1,
  input  [3:0] in_2,
  output [6:0] out_3
);

  wire _0_1_out, _0_2_out, _1_0_out, _1_1_out, _1_2_out, _2_0_out, _2_1_out, _2_2_out, adder_1_cout,
       adder_2_cout, adder_4_cout, adder_4_out, adder_5_cout, adder_5_out, adder_6_cout, adder_7_cout,
       adder_7_out;

  and _0_0 (out_3[0], in_1[0], in_2[0]);
  and _1_0 (_1_0_out, in_1[0], in_2[1]);
  and _2_0 (_2_0_out, in_1[0], in_2[2]);
  and _0_1 (_0_1_out, in_1[1], in_2[0]);
  and _1_1 (_1_1_out, in_1[1], in_2[1]);
  and _2_1 (_2_1_out, in_1[1], in_2[2]);
  and _0_2 (_0_2_out, in_1[2], in_2[0]);
  and _1_2 (_1_2_out, in_1[2], in_2[1]);
  and _2_2 (_2_2_out, in_1[2], in_2[2]);
  Adder #(.width(1)) adder_1 (.a(_1_0_out), .b(_0_1_out), .out(out_3[1]), .cin(1'b0), .cout(adder_1_cout));
  Adder #(.width(1)) adder_2 (.a(_2_1_out), .b(_1_2_out), .out(out_3[3]), .cin(adder_7_out), .cout(adder_2_cout));
  Adder #(.width(1)) adder_3 (.a(adder_7_cout), .b(_2_2_out), .out(out_3[4]), .cin(adder_2_cout), .cout(out_3[5]));
  Adder #(.width(1)) adder_4 (.a(adder_1_cout), .b(_2_0_out), .out(adder_4_out), .cin(1'b0), .cout(adder_4_cout));
  Adder #(.width(1)) adder_5 (.a(_1_1_out), .b(_0_2_out), .out(adder_5_out), .cin(1'b0), .cout(adder_5_cout));
  Adder #(.width(1)) adder_6 (.a(adder_4_out), .b(adder_5_out), .out(out_3[2]), .cin(1'b0), .cout(adder_6_cout));
  Adder #(.width(1)) adder_7 (
    .a(adder_4_cout), .b(adder_5_cout), .out(adder_7_out), .cin(adder_6_cout), .cout(adder_7_cout));
  xor xor_1 (out_3[6], in_1[3], in_2[3]);
endmodule
