// Logisim project Logic Project Final.circ as structural Verilog: 12 circuits, main circuit main
module main (
  input  A,
  input  _4,
  input  _2,
  input  _1,
  input  [1:0] OP,
  input  B,
  input  _4_2,
  input  _2_2,
  input  _1_2,
  output Sign,
  output Zero,
  output Div_by_Zero
);

  wire n7448_1_p10, n7448_1_p11, n7448_1_p12, n7448_1_p13, n7448_1_p14, n7448_1_p15, n7448_1_p16,
       n7448_2_p10, n7448_2_p11, n7448_2_p12, n7448_2_p13, n7448_2_p14, n7448_2_p15, n7448_2_p16,
       n7448_3_p10, n7448_3_p11, n7448_3_p12, n7448_3_p13, n7448_3_p14, n7448_3_p15, n7448_3_p16;
  wire [3:0] binary_2_bcd_1_tenth, binary_2_bcd_1_units;
  wire [6:0] alu_1_result;

  ALU alu_1 (
    .A({A, _4, _2, _1}), .B({B, _4_2, _2_2, _1_2}), .Result(alu_1_result), .in_1(OP), .Zero(Zero),
    .Div__by_Zero(Div_by_Zero));
  Binary_2_BCD binary_2_bcd_1 (
    .sign(Sign), .Units(binary_2_bcd_1_units), .Tenth(binary_2_bcd_1_tenth), .Binary_in(alu_1_result));
  // _7448 7448_1: pin names not known; wires that end beside it: 1'b0, 1'b0, 1'b1, 1'b1, 1'b1, 1'b0, Sign, 1'b0, 1'b1, n7448_1_p10, n7448_1_p11, n7448_1_p12, n7448_1_p13, n7448_1_p14, n7448_1_p15, n7448_1_p16
  // _7448 7448_2: pin names not known; wires that end beside it: binary_2_bcd_1_tenth[1], binary_2_bcd_1_tenth[2], 1'b1, 1'b1, 1'b1, binary_2_bcd_1_tenth[3], binary_2_bcd_1_tenth[0], 1'b0, 1'b1, n7448_2_p10, n7448_2_p11, n7448_2_p12, n7448_2_p13, n7448_2_p14, n7448_2_p15, n7448_2_p16
  // _7448 7448_3: pin names not known; wires that end beside it: binary_2_bcd_1_units[1], binary_2_bcd_1_units[2], 1'b1, 1'b1, 1'b1, binary_2_bcd_1_units[3], binary_2_bcd_1_units[0], 1'b0, 1'b1, n7448_3_p10, n7448_3_p11, n7448_3_p12, n7448_3_p13, n7448_3_p14, n7448_3_p15, n7448_3_p16
  _7_Segment_Display u_7_segment_display_1 (
    .g(n7448_1_p11), .f(n7448_1_p10), .a(n7448_1_p12), .b(n7448_1_p13), .e(n7448_1_p16), .d(n7448_1_p15),
    .c(n7448_1_p14));  // open: dp
  _7_Segment_Display u_7_segment_display_2 (
    .g(n7448_2_p11), .f(n7448_2_p10), .a(n7448_2_p12), .b(n7448_2_p13), .e(n7448_2_p16), .d(n7448_2_p15),
    .c(n7448_2_p14));  // open: dp
  _7_Segment_Display u_7_segment_display_3 (
    .g(n7448_3_p11), .f(n7448_3_p10), .a(n7448_3_p12), .b(n7448_3_p13), .e(n7448_3_p16), .d(n7448_3_p15),
    .c(n7448_3_p14));  // open: dp
  _7_Segment_Display u_7_segment_display_4 (.g(Sign));  // open: f, a, b, e, d, c, dp

  // Notes on the sheet:
  //   sign
  //   sign
  //   0 0=Add
  //   0 1=Sub
  //   1 0=Mult
  //   1 1=Div
  //   Sign Digit
endmodule

module ALU (
  input  [1:0] in_1,
  input  [3:0] A,
  input  [3:0] B,
  output Div__by_Zero,
  output [6:0] Result,
  output Zero
);

  wire add_sub_1_sign, n7404_1_p3, n7404_1_p4, n7408_1_p3, n7408_1_p5, n7408_1_p8, n7408_1_p9, n7432_1_p3,
       n7432_1_p6, n7432_1_p11, n7432_1_p14, n7432_2_p1, n74157_3_p4, n74157_3_p7, n74157_3_p12, n74157_4_p5,
       n74157_4_p8, n74157_4_p10, n74157_4_p15, remainder_1_sign;
  wire [2:0] remainder_1_out_6;
  wire [3:0] add_sub_1_num;
  wire [6:0] multiplication_1_result, n7432_1_p9;

  // _7408 7408_1: pin names not known; wires that end beside it: in_1[1], in_1[0], n7408_1_p3, n7408_1_p3, n7408_1_p5, Div__by_Zero, n7408_1_p3, n7408_1_p8, n7408_1_p9
  // _7404 7404_1: pin names not known; wires that end beside it: 1'b0, 1'b1, n7404_1_p3, n7404_1_p4
  // _7432 7432_1: pin names not known; wires that end beside it: Div__by_Zero, n7408_1_p9, n7432_1_p3, n7432_1_p9[5], n7432_1_p9[4], n7432_1_p6, 1'b0, 1'b1, n7432_1_p9[0], n7432_1_p9[1], n7432_1_p11, n7432_1_p9[2], n7432_1_p9[3], n7432_1_p14
  // _7432 7432_2: pin names not known; wires that end beside it: n7432_2_p1, n7432_1_p6, n7404_1_p3, n7404_1_p4, n7432_1_p3, Zero, 1'b0, 1'b1, n7432_1_p14, n7432_1_p11, n7432_2_p1
  Add_Sub add_sub_1 (.A(A), .B(B), .Num(add_sub_1_num), .sign(add_sub_1_sign), .Op(in_1));
  Multiplication multiplication_1 (.Result(multiplication_1_result), .B(B), .A(A));
  Remainder remainder_1 (
    .A(A), .B(B), .Zero(n7408_1_p8), .Div_by_0(n7408_1_p5), .sign(remainder_1_sign), .out_6(remainder_1_out_6));
  // _74157 74157_1: pin names not known; wires that end beside it: Zero, n7432_1_p9[0], 1'b0, Result[0], n7432_1_p9[1], 1'b0, 1'b1, 1'b0, n7432_1_p9[6], 1'b0, Result[6]
  // _74157 74157_2: pin names not known; wires that end beside it: Result[1], 1'b0, Zero, n7432_1_p9[2], 1'b0, Result[2], n7432_1_p9[3], 1'b0, Result[3], 1'b0, 1'b0, 1'b1, 1'b0, n7432_1_p9[5], 1'b0, Result[5], n7432_1_p9[4], 1'b0, Result[4]
  // _74157 74157_3: pin names not known; wires that end beside it: in_1[0], multiplication_1_result[6], remainder_1_sign, n74157_3_p4, multiplication_1_result[0], remainder_1_out_6[0], n74157_3_p7, 1'b1, 1'b0, multiplication_1_result[1], remainder_1_out_6[1], n74157_3_p12, multiplication_1_result[2], remainder_1_out_6[2]
  // _74157 74157_4: pin names not known; wires that end beside it: 1'b0, in_1[0], multiplication_1_result[3], 1'b0, n74157_4_p5, multiplication_1_result[4], 1'b0, n74157_4_p8, 1'b0, n74157_4_p10, 1'b1, 1'b0, multiplication_1_result[5], 1'b0, n74157_4_p15
  // _74157 74157_5: pin names not known; wires that end beside it: in_1[1], add_sub_1_sign, n74157_3_p4, n7432_1_p9[6], add_sub_1_num[0], n74157_3_p7, 1'b1, 1'b0, add_sub_1_num[1], n74157_3_p12, n7432_1_p9[1], add_sub_1_num[2]
  // _74157 74157_6: pin names not known; wires that end beside it: n7432_1_p9[0], 1'b0, in_1[1], add_sub_1_num[3], n74157_4_p5, n7432_1_p9[3], 1'b0, n74157_4_p8, n7432_1_p9[4], 1'b0, n74157_4_p10, n7432_1_p9[2], 1'b1, 1'b0, 1'b0, n74157_4_p15, n7432_1_p9[5]
endmodule

module Add (
  input  IN,
  input  [2:0] A,
  input  [2:0] B,
  output [3:0] out_4
);

  // _7483 7483_1: pin names not known; wires that end beside it: 1'b0, 1'b0, out_4[3], out_4[2], A[2], IN, B[2], 1'b0, 1'b1, B[0], out_4[1], A[0], B[1], out_4[0], A[1]
endmodule

module Multiplication (
  input  [3:0] A,
  input  [3:0] B,
  output [6:0] Result
);

  wire n7408_1_p9, n7408_2_p1, n7408_2_p5, n7408_2_p9, n7408_2_p13, n7408_3_p1, n7408_3_p5, n7408_3_p8,
       n7483_e_1__2__s3, n7483_e_1__6__s2, n7483_e_1__9__s1, n7483_e_1__15__s4;

  // _7408 7408_1: pin names not known; wires that end beside it: A[0], B[0], Result[0], B[1], A[0], 1'b1, B[0], A[2], n7408_1_p9, B[1]
  // _7408 7408_2: pin names not known; wires that end beside it: n7408_2_p1, 1'b0, A[0], B[2], n7408_2_p5, A[1], B[0], A[2], n7408_2_p9, 1'b1, B[2], A[2], n7408_2_p13
  // _7408 7408_3: pin names not known; wires that end beside it: n7408_3_p1, 1'b0, A[1], B[1], n7408_3_p5, A[1], B[2], n7408_3_p8, 1'b0, 1'b1
  _7483_E u_7483_e_1 (
    ._1__A4(1'b0), ._2__S3(n7483_e_1__2__s3), ._3__A3(1'b0), ._4__B3(n7408_3_p8), ._5__Vcc(1'b1),
    ._6__S2(n7483_e_1__6__s2), ._7__B2(n7408_3_p5), ._8__A2(n7408_2_p5), ._16__B4(1'b0),
    ._15__S4(n7483_e_1__15__s4), ._13__Cin(1'b0), ._12__GND(1'b0), ._11__B1(n7408_3_p1),
    ._10__A1(n7408_2_p1), ._9__S1(n7483_e_1__9__s1));  // open: _14__Cout
  _7483_E u_7483_e_2 (
    ._1__A4(n7408_2_p13), ._2__S3(Result[3]), ._3__A3(n7483_e_1__2__s3), ._4__B3(n7408_2_p9), ._5__Vcc(1'b1),
    ._6__S2(Result[2]), ._7__B2(n7408_1_p9), ._8__A2(n7483_e_1__6__s2), ._16__B4(n7483_e_1__15__s4),
    ._15__S4(Result[4]), ._14__Cout(Result[5]), ._13__Cin(1'b0), ._12__GND(1'b0), ._11__B1(1'b0),
    ._10__A1(n7483_e_1__9__s1), ._9__S1(Result[1]));
  // _7486 7486_1: pin names not known; wires that end beside it: A[3], B[3], Result[6], 1'b0, 1'b1
endmodule

module Sub (
  input  [2:0] A,
  input  [2:0] B,
  output Ind,
  output [2:0] out_4
);

  wire [2:0] n7404_1_p2;

  // _7404 7404_1: pin names not known; wires that end beside it: B[0], n7404_1_p2[0], B[1], n7404_1_p2[1], B[2], n7404_1_p2[2], 1'b0, 1'b1, 1'b1
  Add add_1 (.out_4({Ind, out_4}), .B(n7404_1_p2), .A(A), .IN(1'b1));
endmodule

module Add_Sub (
  input  [1:0] Op,
  input  [3:0] A,
  input  [3:0] B,
  output [3:0] Num,
  output sign
);

  wire n7404_1_p2, n7404_1_p4, n7404_1_p8, n7404_1_p10, n7404_1_p12, n7486_1_p3, n7486_1_p6, n7486_1_p11,
       n74157_1_p4, n74157_1_p7, n74157_1_p13;
  wire [2:0] n7486_2_p11;
  wire [3:0] add_2_out_4, n7486_1_p10;

  // _7486 7486_1: pin names not known; wires that end beside it: Op[0], A[3], n7486_1_p3, n7486_1_p3, B[3], n7486_1_p6, 1'b0, 1'b1, A[3], n7486_1_p10[3], n7486_1_p11
  // _7486 7486_2: pin names not known; wires that end beside it: B[2], n7486_1_p6, n7486_2_p11[2], B[1], n7486_1_p6, n7486_2_p11[1], 1'b0, 1'b1, B[0], n7486_1_p6, n7486_2_p11[0]
  Add add_1 (.out_4(n7486_1_p10), .B(n7486_2_p11), .A(A[2:0]), .IN(1'b0));
  // _7404 7404_1: pin names not known; wires that end beside it: n7486_1_p6, n7404_1_p2, n7486_1_p11, n7404_1_p4, 1'b0, 1'b1, n7486_1_p10[0], n7404_1_p8, n7486_1_p10[1], n7404_1_p10, n7486_1_p10[2], n7404_1_p12
  Add add_2 (.out_4(add_2_out_4), .B(3'b000), .A(n7486_1_p10[2:0]), .IN(n7486_1_p10[3]));
  // _74157 74157_1: pin names not known; wires that end beside it: n7486_1_p10[3], n7404_1_p8, add_2_out_4[0], n74157_1_p4, n7404_1_p10, add_2_out_4[1], n74157_1_p7, 1'b0, 1'b1, 1'b0, n7404_1_p12, add_2_out_4[2], n74157_1_p13
  // _74157 74157_2: pin names not known; wires that end beside it: n7486_1_p6, A[3], n7404_1_p4, sign, n7486_1_p10[0], n74157_1_p4, Num[0], 1'b0, 1'b1, 1'b0, n7486_1_p10[2], n74157_1_p13, Num[2], n7486_1_p10[1], n74157_1_p7, Num[1]
  // _7408 7408_1: pin names not known; wires that end beside it: n7486_1_p10[3], n7404_1_p2, Num[3], 1'b0, 1'b1
endmodule

module Remainder (
  input  [3:0] A,
  input  [3:0] B,
  output Zero,
  output Div_by_0,
  output sign,
  output [2:0] out_6
);

  wire n74157_1_p3, n74157_2_p1, n74157_2_p6, n74157_2_p10, n74157_3_p1, n74157_3_p13, sub_1_ind, sub_2_ind,
       sub_3_ind;
  wire [2:0] sub_1_out_4, sub_2_out_4, sub_3_out_4;

  Zero_flag zero_flag_1 (.IN(B), .One(Zero), .Zero(Div_by_0));
  Sub sub_1 (.A(A[2:0]), .B(B[2:0]), .out_4(sub_1_out_4), .Ind(sub_1_ind));
  Sub sub_2 (.A(sub_1_out_4), .B(B[2:0]), .out_4(sub_2_out_4), .Ind(sub_2_ind));
  Sub sub_3 (.A(sub_2_out_4), .B(B[2:0]), .out_4(sub_3_out_4), .Ind(sub_3_ind));
  // _74157 74157_1: pin names not known; wires that end beside it: sub_1_ind, A[0], n74157_1_p3, out_6[0], A[1], 1'b1, 1'b0
  // _74157 74157_2: pin names not known; wires that end beside it: n74157_2_p1, out_6[1], 1'b0, sub_2_ind, sub_1_out_4[0], n74157_2_p6, n74157_1_p3, sub_1_out_4[1], A[2], n74157_2_p10, out_6[2], 1'b1, 1'b0
  // _74157 74157_3: pin names not known; wires that end beside it: n74157_3_p1, n74157_2_p1, 1'b0, sub_3_ind, sub_2_out_4[0], sub_3_out_4[0], n74157_2_p6, sub_2_out_4[1], sub_3_out_4[1], n74157_3_p1, 1'b0, sub_1_out_4[2], n74157_3_p13, n74157_2_p10, 1'b1, 1'b0, sub_2_out_4[2], sub_3_out_4[2], n74157_3_p13

  assign sign = A[3];
endmodule

module Zero_flag (
  input  [3:0] IN,
  output One,
  output Zero
);

  wire n7432_1_p3, n7432_1_p6;

  // _7432 7432_1: pin names not known; wires that end beside it: IN[1], IN[2], n7432_1_p3, n7432_1_p3, IN[0], n7432_1_p6, 1'b0, 1'b1
  // _7404 7404_1: pin names not known; wires that end beside it: 1'b1, n7432_1_p6, n7432_1_p3, Zero, One, 1'b0
endmodule

module Binary_2_BCD (
  input  [6:0] Binary_in,
  output sign,
  output [3:0] Units,
  output [3:0] Tenth
);

  wire bcd_add_2_cout, bcd_add_3_cout, bcd_sub_1_ind, bcd_sub_2_ind, bcd_sub_3_ind, n7404_1_p3, n7404_1_p4,
       n7404_1_p5, n7404_1_p6, n7408_1_p3, n7408_1_p8, n7432_2_p3, n74157_2_p1;
  wire [2:0] bcd_add_1_out, bcd_add_2_out, bcd_add_3_out;
  wire [2:1] n7432_1_p5, n74157_1_p4;

  BCD_sub bcd_sub_1 (.A(Binary_in[5:3]), .B(3'b100), .Ind(bcd_sub_1_ind));
  BCD_Add bcd_add_1 (.Out(bcd_add_1_out), .Cout(Tenth[2]), .B(3'b011), .A(Binary_in[5:3]));
  // _74157 74157_1: pin names not known; wires that end beside it: bcd_sub_1_ind, Binary_in[3], bcd_add_1_out[0], n74157_1_p4[1], Binary_in[4], bcd_add_1_out[1], n74157_1_p4[2], 1'b0, 1'b0
  // _7404 7404_1: pin names not known; wires that end beside it: 1'b0, 1'b1, n7404_1_p3, n7404_1_p4, n7404_1_p5, n7404_1_p6, 1'b0
  // _7432 7432_1: pin names not known; wires that end beside it: n74157_1_p4[1], n74157_1_p4[2], n7404_1_p3, 1'b1, n7432_1_p5[1], n7432_1_p5[2], n7404_1_p5
  BCD_sub bcd_sub_2 (.A({n74157_1_p4, Binary_in[2]}), .B(3'b100), .Ind(bcd_sub_2_ind));
  BCD_Add bcd_add_2 (.Out(bcd_add_2_out), .Cout(bcd_add_2_cout), .B(3'b011), .A({n74157_1_p4, Binary_in[2]}));
  // _74157 74157_2: pin names not known; wires that end beside it: n74157_2_p1, Binary_in[2], bcd_add_2_out[0], n7432_1_p5[1], n74157_1_p4[1], bcd_add_2_out[1], n7432_1_p5[2], 1'b0
  BCD_Add bcd_add_3 (.Out(bcd_add_3_out), .Cout(bcd_add_3_cout), .B(3'b011), .A({n7432_1_p5, Binary_in[1]}));
  // _7408 7408_1: pin names not known; wires that end beside it: n7404_1_p4, bcd_add_1_out[2], n7408_1_p3, 1'b0, 1'b1, bcd_add_2_out[2], n7404_1_p6, n7408_1_p8
  BCD_sub bcd_sub_3 (.A({n7432_1_p5, Binary_in[1]}), .B(3'b100), .Ind(bcd_sub_3_ind));
  // _7432 7432_2: pin names not known; wires that end beside it: 1'b0, Tenth[1], n7432_2_p3, n7408_1_p3, bcd_sub_3_ind, bcd_add_2_cout, n7408_1_p8, n74157_2_p1, Tenth[0], n7408_1_p3, bcd_add_3_cout, bcd_sub_2_ind, n7408_1_p8, 1'b1
  // _74157 74157_3: pin names not known; wires that end beside it: n7432_2_p3, Binary_in[1], bcd_add_3_out[0], Units[1], n7432_1_p5[1], bcd_add_3_out[1], Units[2], 1'b0, n7432_1_p5[2], bcd_add_3_out[2], Units[3]

  assign sign = Binary_in[6];
  assign Tenth[3] = 1'b0;
  assign Units[0] = Binary_in[0];
endmodule

module BCD_sub (
  input  [2:0] A,
  input  [2:0] B,
  output Ind
);

  wire [2:0] add_1_out_4, n7404_1_p2;

  // _7404 7404_1: pin names not known; wires that end beside it: B[0], n7404_1_p2[0], B[1], n7404_1_p2[1], B[2], n7404_1_p2[2], 1'b0, 1'b1, 1'b0
  Add add_1 (.out_4({Ind, add_1_out_4}), .B(n7404_1_p2), .A(A), .IN(1'b0));
endmodule

module BCD_Add (
  input  [2:0] A,
  input  [2:0] B,
  output [2:0] Out,
  output Cout
);

  // _7483 7483_1: pin names not known; wires that end beside it: 1'b0, 1'b0, Cout, Out[2], A[2], 1'b0, B[2], 1'b0, 1'b1, B[0], Out[1], A[0], B[1], Out[0], A[1]
endmodule

module _7483_E (
  input  _1__A4,
  input  _16__B4,
  input  _3__A3,
  input  _4__B3,
  input  _13__Cin,
  input  _5__Vcc,
  input  _12__GND,
  input  _11__B1,
  input  _7__B2,
  input  _10__A1,
  input  _8__A2,
  output _2__S3,
  output _15__S4,
  output _14__Cout,
  output _6__S2,
  output _9__S1
);

  wire and_1_out, and_2_out, and_3_out, and_4_out, and_5_out, and_6_out, and_7_out, and_8_out, and_9_out,
       and_10_out, and_11_out, and_12_out, and_13_out, and_14_out, nand_1_out, nand_2_out, nand_3_out,
       nand_4_out, nor_1_out, nor_2_out, nor_3_out, nor_4_out, nor_6_out, nor_7_out, nor_8_out, not_1_out,
       not_2_out, not_3_out, not_4_out, not_5_out, not_6_out;

  nand nand_1 (nand_1_out, _16__B4, _1__A4);
  nor nor_1 (nor_1_out, _16__B4, _1__A4);
  nand nand_2 (nand_2_out, _4__B3, _3__A3);
  nor nor_2 (nor_2_out, _4__B3, _3__A3);
  nand nand_3 (nand_3_out, _7__B2, _8__A2);
  nor nor_3 (nor_3_out, _7__B2, _8__A2);
  nand nand_4 (nand_4_out, _11__B1, _10__A1);
  nor nor_4 (nor_4_out, _11__B1, _10__A1);
  and and_1 (and_1_out, nor_2_out, nand_1_out);
  and and_2 (and_2_out, nor_3_out, nand_1_out, nand_2_out);
  and and_3 (and_3_out, nor_4_out, nand_1_out, nand_2_out, nand_3_out);
  and and_4 (and_4_out, nand_1_out, nand_2_out, nand_3_out, nand_4_out, not_2_out);
  not not_1 (not_1_out, nor_1_out);
  and and_5 (and_5_out, nor_3_out, nand_2_out);
  and and_6 (and_6_out, nor_4_out, nand_2_out, nand_3_out);
  and and_7 (and_7_out, nand_2_out, nand_3_out, nand_4_out, not_2_out);
  not not_2 (not_2_out, _13__Cin);
  not not_3 (not_3_out, nor_2_out);
  and and_8 (and_8_out, nor_4_out, nand_3_out);
  and and_9 (and_9_out, nand_3_out, nand_4_out, not_2_out);
  not not_4 (not_4_out, nor_3_out);
  and and_10 (and_10_out, nand_4_out, not_2_out);
  not not_5 (not_5_out, nor_4_out);
  not not_6 (not_6_out, not_2_out);
  nor nor_5 (_14__Cout, nor_1_out, and_1_out, and_2_out, and_3_out, and_4_out);
  and and_11 (and_11_out, nand_1_out, not_1_out);
  and and_12 (and_12_out, nand_2_out, not_3_out);
  and and_13 (and_13_out, nand_3_out, not_4_out);
  and and_14 (and_14_out, nand_4_out, not_5_out);
  xor xor_1 (_15__S4, and_11_out, nor_6_out);
  nor nor_6 (nor_6_out, nor_2_out, and_5_out, and_6_out, and_7_out);
  xor xor_2 (_2__S3, and_12_out, nor_7_out);
  nor nor_7 (nor_7_out, nor_3_out, and_8_out, and_9_out);
  xor xor_3 (_6__S2, and_13_out, nor_8_out);
  nor nor_8 (nor_8_out, nor_4_out, and_10_out);
  xor xor_4 (_9__S1, and_14_out, not_6_out);

  // Notes on the sheet:
  //   7483: 4-bit full adder
endmodule
