// Logisim project To7-segment.circ as structural Verilog: 8 circuits, main circuit main
module main (
  input  [3:0] in_1,
  output out_2,
  output out_3,
  output out_4,
  output out_5,
  output out_6,
  output out_7,
  output out_8
);

  middle middle_1 (.in_1(in_1), .out_2(out_2));
  top_left top_left_1 (.in_1(in_1), .out_2(out_3));
  top top_1 (.in_1(in_1), .out_2(out_4));
  top_right top_right_1 (.in_1(in_1), .out_2(out_5));
  bottom_left bottom_left_1 (.in_1(in_1), .out_2(out_6));
  bottom bottom_1 (.in_1(in_1), .out_2(out_7));
  bottom_right bottom_right_1 (.in_1(in_1), .out_2(out_8));
endmodule

module middle (
  input  [3:0] in_1,
  output out_2
);

  wire and_1_out, and_2_out, nand_1_out, not_1_out, or_1_out, or_3_out;

  or or_1 (or_1_out, in_1[3], in_1[2]);
  not not_1 (not_1_out, in_1[1]);
  nand nand_1 (nand_1_out, or_1_out, in_1[0]);
  and and_1 (and_1_out, not_1_out, in_1[2]);
  and and_2 (and_2_out, nand_1_out, in_1[1]);
  or or_2 (out_2, and_2_out, or_3_out);
  or or_3 (or_3_out, and_1_out, in_1[3]);
endmodule

module top_left (
  input  [3:0] in_1,
  output out_2
);

  wire and_1_out, nand_1_out, nor_1_out, or_2_out;

  nand nand_1 (nand_1_out, in_1[0], in_1[1]);
  nor nor_1 (nor_1_out, in_1[0], in_1[1]);
  and and_1 (and_1_out, nand_1_out, in_1[2]);
  or or_1 (out_2, nor_1_out, or_2_out);
  or or_2 (or_2_out, and_1_out, in_1[3]);
endmodule

module top (
  input  [3:0] in_1,
  output out_2
);

  wire and_1_out, nor_1_out, or_1_out, or_2_out, or_3_out;

  and and_1 (and_1_out, in_1[2], in_1[0]);
  nor nor_1 (nor_1_out, in_1[0], or_1_out);
  or or_1 (or_1_out, in_1[2], in_1[3]);
  or or_2 (or_2_out, in_1[1], in_1[3]);
  or or_3 (or_3_out, nor_1_out, or_2_out);
  or or_4 (out_2, and_1_out, or_3_out);
endmodule

module top_right (
  input  [3:0] in_1,
  output out_2
);

  wire and_1_out, nor_1_out, nor_2_out, or_1_out, or_2_out;

  and and_1 (and_1_out, in_1[1], in_1[0]);
  nor nor_1 (nor_1_out, in_1[0], in_1[1]);
  or or_1 (or_1_out, in_1[3], nor_2_out);
  nor nor_2 (nor_2_out, in_1[3], in_1[2]);
  or or_2 (or_2_out, and_1_out, nor_1_out);
  or or_3 (out_2, or_2_out, or_1_out);
endmodule

module bottom_left (
  input  [3:0] in_1,
  output out_2
);

  wire and_1_out, nor_1_out, not_1_out, not_2_out, or_1_out;

  not not_1 (not_1_out, in_1[3]);
  nor nor_1 (nor_1_out, in_1[1], in_1[2]);
  and and_1 (and_1_out, in_1[1], not_1_out);
  not not_2 (not_2_out, in_1[0]);
  or or_1 (or_1_out, nor_1_out, and_1_out);
  and and_2 (out_2, not_2_out, or_1_out);
endmodule

module bottom (
  input  [3:0] in_1,
  output out_2
);

  wire and_1_out, nand_1_out, nor_1_out, or_1_out, xor_1_out;

  xor xor_1 (xor_1_out, in_1[0], in_1[2]);
  nand nand_1 (nand_1_out, in_1[2], in_1[0]);
  and and_1 (and_1_out, nand_1_out, in_1[1]);
  nor nor_1 (nor_1_out, in_1[1], xor_1_out);
  or or_1 (or_1_out, and_1_out, nor_1_out);
  or or_2 (out_2, or_1_out, in_1[3]);
endmodule

module bottom_right (
  input  [3:0] in_1,
  output out_2
);

  wire and_1_out, not_1_out, not_2_out, or_1_out, or_2_out;

  not not_1 (not_1_out, in_1[1]);
  or or_1 (or_1_out, in_1[0], not_1_out);
  or or_2 (or_2_out, or_1_out, in_1[2]);
  not not_2 (not_2_out, in_1[3]);
  and and_1 (and_1_out, or_2_out, not_2_out);
  or or_3 (out_2, and_1_out, in_1[3]);
endmodule
