// Logisim project ALU.circ as structural Verilog: 10 circuits, main circuit main
module main (
  input  [1:0] in_1,
  input  [3:0] A,
  input  [3:0] B,
  output [6:0] Result,
  output Zero,
  output Div__by_Zero
);

  wire add_sub_1_zero, and_1_out, division_1_div__by_zero, division_1_zero, multiplication_1_zero;
  wire [6:0] add_sub_1_out, division_1_out, multiplication_1_result;

  and and_1 (and_1_out, in_1[1], in_1[0]);
  and and_2 (Div__by_Zero, division_1_div__by_zero, and_1_out);
  Multiplication multiplication_1 (.Result(multiplication_1_result), .Zero(multiplication_1_zero), .B(B), .A(A));
  Division division_1 (
    .A(A), .B(B), .Div__by_zero(division_1_div__by_zero), .Out(division_1_out), .Zero(division_1_zero));
  Add_Sub add_sub_1 (.Op(in_1), .A(A), .B(B), .Out(add_sub_1_out), .Zero(add_sub_1_zero));
  Multiplexer #(.select(2), .enable("false")) multiplexer_1 (
    .in0(add_sub_1_zero), .in1(add_sub_1_zero), .in2(multiplication_1_zero), .in3(division_1_zero),
    .out(Zero), .sel(in_1));
  Multiplexer #(.select(2), .width(7), .enable("false")) multiplexer_2 (
    .in0(add_sub_1_out), .in1(add_sub_1_out), .in2(multiplication_1_result), .in3(division_1_out),
    .out(Result), .sel(in_1));
endmodule

module ALU (
  input  [1:0] in_1,
  input  [3:0] A,
  input  [3:0] B,
  output [6:0] Result,
  output Zero,
  output Div__by_Zero
);

  wire add_sub_1_zero, division_1_zero, multiplication_1_zero, or_1_out;
  wire [6:0] add_sub_1_out, division_1_out, multiplication_1_result;

  Multiplication multiplication_1 (.Result(multiplication_1_result), .Zero(multiplication_1_zero), .B(B), .A(A));
  Division division_1 (.A(A), .B(B), .Div__by_zero(Div__by_Zero), .Out(division_1_out), .Zero(division_1_zero));
  Add_Sub add_sub_1 (.Op(in_1), .A(A), .B(B), .Out(add_sub_1_out), .Zero(add_sub_1_zero));
  or or_1 (or_1_out, add_sub_1_zero, multiplication_1_zero);
  or or_2 (Zero, or_1_out, division_1_zero);
  Multiplexer #(.select(2), .width(7), .enable("false")) multiplexer_1 (
    .in0(add_sub_1_out), .in1(add_sub_1_out), .in2(multiplication_1_result), .in3(division_1_out),
    .out(Result), .sel(in_1));
endmodule

module Add_Sub (
  input  [1:0] Op,
  input  [3:0] A,
  input  [3:0] B,
  output [6:0] Out,
  output Zero
);

  wire multiplexer_1_out, not_1_out, sub_1_ind, xnor_1_out, xor_1_out, xor_2_out;
  wire [3:0] add_1_out_4, sub_1_out_4;

  xor xor_1 (xor_1_out, Op[0], xor_2_out);
  xor xor_2 (xor_2_out, A[3], B[3]);
  Add add_1 (.out_4(add_1_out_4), .B(B[2:0]), .A(A[2:0]));  // open: in_3
  Sub sub_1 (.A(A[2:0]), .B(B[2:0]), .out_4(sub_1_out_4), .Ind(sub_1_ind));  // open: Flag
  Multiplexer #(.enable("false")) multiplexer_1 (
    .in0(A[3]), .in1(xnor_1_out), .out(multiplexer_1_out), .sel(xor_1_out));
  xnor xnor_1 (xnor_1_out, A[3], sub_1_ind);
  Multiplexer #(.width(4), .enable("false")) multiplexer_2 (
    .in0(add_1_out_4), .in1(sub_1_out_4), .out(Out[3:0]), .sel(xor_1_out));
  Zero_flag zero_flag_1 (.in_1(Out[3:0]), .out_2(Zero));
  and and_1 (Out[6], multiplexer_1_out, not_1_out);
  not not_1 (not_1_out, Zero);

  assign Out[5:4] = 2'b00;
endmodule

module Multiplication (
  input  [3:0] A,
  input  [3:0] B,
  output [6:0] Result,
  output Zero
);

  wire _0_1_out, _0_2_out, _1_0_out, _1_1_out, _1_2_out, _2_0_out, _2_1_out, _2_2_out, adder_1_cout,
       adder_2_cout, adder_2_out, adder_3_cout, adder_5_cout, adder_5_out, adder_6_cout, adder_7_cout,
       adder_7_out, zero_flag_1_out_2, zero_flag_2_out_2;
  wire [3:0] adder_6_out;
  wire [6:0] _0_0_out;

  and _0_0 (_0_0_out[0], A[0], B[0]);
  and _1_0 (_1_0_out, A[0], B[1]);
  and _2_0 (_2_0_out, A[0], B[2]);
  and _0_1 (_0_1_out, A[1], B[0]);
  and _1_1 (_1_1_out, A[1], B[1]);
  and _2_1 (_2_1_out, A[1], B[2]);
  and _0_2 (_0_2_out, A[2], B[0]);
  and _1_2 (_1_2_out, A[2], B[1]);
  and _2_2 (_2_2_out, A[2], B[2]);
  Adder #(.width(1)) adder_1 (.a(_1_0_out), .b(_0_1_out), .out(_0_0_out[1]), .cin(1'b0), .cout(adder_1_cout));
  Adder #(.width(1)) adder_2 (.a(adder_1_cout), .b(_2_0_out), .out(adder_2_out), .cin(1'b0), .cout(adder_2_cout));
  Adder #(.width(1)) adder_3 (.a(_2_1_out), .b(_1_2_out), .out(adder_6_out[2]), .cin(adder_7_out), .cout(adder_3_cout));
  Adder #(.width(1)) adder_4 (
    .a(adder_7_cout), .b(_2_2_out), .out(adder_6_out[1]), .cin(adder_3_cout), .cout(adder_6_out[0]));
  Adder #(.width(1)) adder_5 (.a(_1_1_out), .b(_0_2_out), .out(adder_5_out), .cin(1'b0), .cout(adder_5_cout));
  Adder #(.width(1)) adder_6 (.a(adder_2_out), .b(adder_5_out), .out(adder_6_out[3]), .cin(1'b0), .cout(adder_6_cout));
  Adder #(.width(1)) adder_7 (
    .a(adder_2_cout), .b(adder_5_cout), .out(adder_7_out), .cin(adder_6_cout), .cout(adder_7_cout));
  xor xor_1 (_0_0_out[6], A[3], B[3]);
  Zero_flag zero_flag_1 (.in_1({2'b00, _0_0_out[0], _0_0_out[1]}), .out_2(zero_flag_1_out_2));
  Zero_flag zero_flag_2 (.in_1(adder_6_out), .out_2(zero_flag_2_out_2));
  Multiplexer #(.width(7), .enable("false")) multiplexer_1 (
    .in0({_0_0_out[6], adder_6_out[0], adder_6_out[1], adder_6_out[2], adder_6_out[3], _0_0_out[1:0]}),
    .in1({7{1'b0}}), .out(Result), .sel(Zero));
  and and_1 (Zero, zero_flag_1_out_2, zero_flag_2_out_2);
endmodule

module Division (
  input  [3:0] A,
  input  [3:0] B,
  output Zero,
  output Div__by_zero,
  output [6:0] Out
);

  wire nor_1_out, not_1_out, one_check_1_out_2, or_2_out, or_3_out, sub_1_flag, sub_1_ind, sub_2_flag,
       sub_2_ind, sub_3_flag, sub_3_ind;
  wire [2:0] sub_1_out_4_2;
  wire [3:0] multiplexer_1_out, multiplexer_2_out, multiplexer_3_out, multiplexer_4_out, sub_2_out_4,
       sub_3_out_4;
  wire [3:3] sub_1_out_4;

  or or_1 (Zero, sub_1_flag, or_2_out);
  or or_2 (or_2_out, sub_2_flag, sub_3_flag);
  Zero_flag zero_flag_1 (.in_1(B), .out_2(Div__by_zero));
  one_check one_check_1 (.in_1(B), .out_2(one_check_1_out_2));
  Sub sub_1 (.A(A[2:0]), .B(B[2:0]), .out_4({sub_1_out_4[3], sub_1_out_4_2}), .Ind(sub_1_ind), .Flag(sub_1_flag));
  nor nor_1 (nor_1_out, Zero, Div__by_zero);
  not not_1 (not_1_out, one_check_1_out_2);
  Sub sub_2 (.A(sub_1_out_4_2), .B(B[2:0]), .out_4(sub_2_out_4), .Ind(sub_2_ind), .Flag(sub_2_flag));
  or or_3 (or_3_out, nor_1_out, one_check_1_out_2);
  Multiplexer #(.width(4), .enable("false")) multiplexer_1 (
    .in0({1'b0, sub_1_out_4_2}), .in1(multiplexer_4_out), .out(multiplexer_1_out), .sel(sub_2_ind));
  Sub sub_3 (.A(sub_2_out_4[2:0]), .B(B[2:0]), .out_4(sub_3_out_4), .Ind(sub_3_ind), .Flag(sub_3_flag));
  Multiplexer #(.width(4), .enable("false")) multiplexer_2 (
    .in0({1'b0, A[2:0]}), .in1(multiplexer_1_out), .out(multiplexer_2_out), .sel(sub_1_ind));
  Multiplexer #(.width(4), .enable("false")) multiplexer_3 (
    .in0({1'b0, A[2:0]}), .in1(multiplexer_2_out), .out(multiplexer_3_out), .sel(not_1_out));
  Multiplexer #(.width(4), .enable("false")) multiplexer_4 (
    .in0({1'b0, sub_2_out_4[2:0]}), .in1(sub_3_out_4), .out(multiplexer_4_out), .sel(sub_3_ind));
  Multiplexer #(.width(7), .enable("false")) multiplexer_5 (
    .in0({7{1'b0}}), .in1({A[3], 2'b00, multiplexer_3_out}), .out(Out), .sel(or_3_out));
endmodule

module Sub (
  input  [2:0] A,
  input  [2:0] B,
  output Ind,
  output [3:0] out_4,
  output Flag
);

  wire [2:0] add_1_out_4, complement_1_out_2, complement_2_out_2;
  wire [3:0] add_2_out_4;

  complement complement_1 (.IN(B), .out_2(complement_1_out_2));
  Add add_1 (.out_4({Ind, add_1_out_4}), .B(complement_1_out_2), .A(A));  // open: in_3
  Add add_2 (.out_4(add_2_out_4), .B(3'b000), .A(add_1_out_4), .in_3(Ind));
  complement complement_2 (.IN(add_1_out_4), .out_2(complement_2_out_2));
  Multiplexer #(.width(4), .enable("false")) multiplexer_1 (
    .in0({1'b0, complement_2_out_2}), .in1(add_2_out_4), .out(out_4), .sel(Ind));
  Zero_flag zero_flag_1 (.in_1(out_4), .out_2(Flag));
endmodule

module Add (
  input  [2:0] A,
  input  [2:0] B,
  input  in_3,
  output [3:0] out_4
);

  wire adder_1_cout, adder_2_cout;

  Adder #(.width(1)) adder_1 (.a(A[0]), .b(B[0]), .out(out_4[0]), .cin(in_3), .cout(adder_1_cout));
  Adder #(.width(1)) adder_2 (.a(A[1]), .b(B[1]), .out(out_4[1]), .cin(adder_1_cout), .cout(adder_2_cout));
  Adder #(.width(1)) adder_3 (.a(A[2]), .b(B[2]), .out(out_4[2]), .cin(adder_2_cout), .cout(out_4[3]));
endmodule

module complement (
  input  [2:0] IN,
  output [2:0] out_2
);

  xor xor_1 (out_2[0], IN[0], 1'b1);
  xor xor_2 (out_2[1], IN[1], 1'b1);
  xor xor_3 (out_2[2], IN[2], 1'b1);
endmodule

module Zero_flag (
  input  [3:0] in_1,
  output out_2
);

  wire or_1_out, or_2_out;

  or or_1 (or_1_out, in_1[0], in_1[1]);
  or or_2 (or_2_out, or_1_out, in_1[2]);
  nor nor_1 (out_2, or_2_out, in_1[3]);
endmodule

module one_check (
  input  [3:0] in_1,
  output out_2
);

  wire and_1_out, and_2_out, not_1_out, not_2_out;

  and and_1 (and_1_out, 1'b1, in_1[0]);
  not not_1 (not_1_out, in_1[1]);
  and and_2 (and_2_out, and_1_out, not_1_out);
  not not_2 (not_2_out, in_1[2]);
  and and_3 (out_2, and_2_out, not_2_out);
endmodule
