// Logisim project Adder-Sub.circ as structural Verilog: 4 circuits, main circuit main
module main (
  input  [1:0] Op,
  input  [3:0] A,
  input  [3:0] B,
  output Sign,
  output [3:0] Number,
  output [6:0] Out
);

  wire xnor_1_out, xor_1_out, xor_2_out;
  wire [2:0] complement_1_out_3, complement_2_out_3;
  wire [3:0] add_1_out_4, add_2_out_4, multiplexer_2_out;

  xor xor_1 (xor_1_out, Op[0], xor_2_out);
  xor xor_2 (xor_2_out, A[3], B[3]);
  complement complement_1 (.IN({B[0], B[1], B[2]}), .out_3(complement_1_out_3), .Comp(xor_1_out));
  Add add_1 (.out_4(add_1_out_4), .B(complement_1_out_3), .A({A[0], A[1], A[2]}));  // open: in_3
  Multiplexer #(.enable("false")) multiplexer_1 (.in0(A[3]), .in1(xnor_1_out), .out(Out[6]), .sel(xor_1_out));
  xnor xnor_1 (xnor_1_out, A[3], add_1_out_4[3]);
  Add add_2 (.out_4(add_2_out_4), .B(3'b000), .A(add_1_out_4[2:0]), .in_3(add_1_out_4[3]));
  complement complement_2 (.IN(add_1_out_4[2:0]), .out_3(complement_2_out_3), .Comp(1'b1));
  Multiplexer #(.width(4), .enable("false")) multiplexer_2 (
    .in0({1'b0, complement_2_out_3}), .in1(add_2_out_4), .out(multiplexer_2_out), .sel(add_1_out_4[3]));
  Multiplexer #(.width(4), .enable("false")) multiplexer_3 (
    .in0(add_1_out_4), .in1(multiplexer_2_out), .out(Number), .sel(xor_1_out));

  assign Out[5:0] = {2'b00, Number};
  assign Sign = Out[6];
endmodule

module Add (
  input  [2:0] A,
  input  [2:0] B,
  input  in_3,
  output [3:0] out_4
);

  wire adder_1_cout, adder_2_cout;

  Adder #(.width(1)) adder_1 (.a(A[0]), .b(B[0]), .out(out_4[0]), .cin(in_3), .cout(adder_1_cout));
  Adder #(.width(1)) adder_2 (.a(A[1]), .b(B[1]), .out(out_4[1]), .cin(adder_1_cout), .cout(adder_2_cout));
  Adder #(.width(1)) adder_3 (.a(A[2]), .b(B[2]), .out(out_4[2]), .cin(adder_2_cout), .cout(out_4[3]));
endmodule

module complement (
  input  Comp,
  input  [2:0] IN,
  output [2:0] out_3
);

  xor xor_1 (out_3[0], IN[0], Comp);
  xor xor_2 (out_3[1], IN[1], Comp);
  xor xor_3 (out_3[2], IN[2], Comp);
endmodule

module Sign (
  input  P,
  input  A,
  input  B,
  output out_4
);

  wire and_1_out, not_1_out, or_1_out, xnor_1_out;

  not not_1 (not_1_out, P);
  xnor xnor_1 (xnor_1_out, A, B);
  or or_1 (or_1_out, not_1_out, xnor_1_out);
  and and_1 (and_1_out, P, xnor_1_out);
  or or_2 (out_4, or_1_out, and_1_out);
endmodule
