// Logisim project Logic project.circ as structural Verilog: 1 circuit, main circuit main
module main (
  input  [1:0] Op,
  input  [3:0] A,
  input  [3:0] B,
  output Div__by_Zero,
  output out_5
);

  wire main_2_out_2, main_2_out_3, main_2_out_4, main_2_out_5, main_2_out_6, main_2_out_7, main_2_out_8,
       main_3_out_2, main_3_out_3, main_3_out_4, main_3_out_5, main_3_out_6, main_3_out_7, main_3_out_8,
       n2_bcd_1_out_2;
  wire [3:0] n2_bcd_1_tenth, n2_bcd_1_units;
  wire [6:0] main_1_result;

  ALU_main main_1 (.in_1(Op), .A(A), .B(B), .Div__by_Zero(Div__by_Zero), .Result(main_1_result), .Zero(out_5));
  _2_BCD u_2_bcd_1 (.out_2(n2_bcd_1_out_2), .Binary_in(main_1_result), .Units(n2_bcd_1_units), .Tenth(n2_bcd_1_tenth));
  To7_segment_main main_2 (
    .in_1(n2_bcd_1_tenth), .out_2(main_2_out_2), .out_3(main_2_out_3), .out_4(main_2_out_4),
    .out_5(main_2_out_5), .out_6(main_2_out_6), .out_7(main_2_out_7), .out_8(main_2_out_8));
  To7_segment_main main_3 (
    .in_1(n2_bcd_1_units), .out_2(main_3_out_2), .out_3(main_3_out_3), .out_4(main_3_out_4),
    .out_5(main_3_out_5), .out_6(main_3_out_6), .out_7(main_3_out_7), .out_8(main_3_out_8));
  _7_Segment_Display u_7_segment_display_1 (.g(n2_bcd_1_out_2));  // open: f, a, b, e, d, c, dp
  _7_Segment_Display u_7_segment_display_2 (
    .g(main_2_out_2), .f(main_2_out_3), .a(main_2_out_4), .b(main_2_out_5), .e(main_2_out_6),
    .d(main_2_out_7), .c(main_2_out_8));  // open: dp
  _7_Segment_Display u_7_segment_display_3 (
    .g(main_3_out_2), .f(main_3_out_3), .a(main_3_out_4), .b(main_3_out_5), .e(main_3_out_6),
    .d(main_3_out_7), .c(main_3_out_8));  // open: dp
endmodule
